// Logisim project display.circ as structural Verilog: 1 circuit, main circuit main
module main (
  input  A,
  input  B,
  input  C,
  output S
);

  wire and_1_out;

  and and_1 (and_1_out, B, C);
  or or_1 (S, A, and_1_out);
endmodule
