// Logisim project nota_aluno_display.circ as structural Verilog: 2 circuits, main circuit main
module main (
  input  A,
  input  B,
  input  C,
  input  D
);

  wire nota_aluno_1_a_2, nota_aluno_1_b_2, nota_aluno_1_c_2, nota_aluno_1_d_2, nota_aluno_1_e,
       nota_aluno_1_f, nota_aluno_1_g;

  nota_aluno nota_aluno_1 (
    .A(A), .B(B), .C(C), .D(D), .a_2(nota_aluno_1_a_2), .b_2(nota_aluno_1_b_2), .c_2(nota_aluno_1_c_2),
    .d_2(nota_aluno_1_d_2), .e(nota_aluno_1_e), .f(nota_aluno_1_f), .g(nota_aluno_1_g));
  _7_Segment_Display u_7_segment_display_1 (
    .g(nota_aluno_1_g), .f(nota_aluno_1_f), .a(nota_aluno_1_a_2), .b(nota_aluno_1_b_2), .e(nota_aluno_1_e),
    .d(nota_aluno_1_d_2), .c(nota_aluno_1_c_2));  // open: dp
endmodule

module nota_aluno (
  input  A,
  input  B,
  input  C,
  input  D,
  output a_2,
  output b_2,
  output c_2,
  output d_2,
  output e,
  output f,
  output g
);

  wire and_1_out, and_2_out, not_1_out;

  not not_1 (not_1_out, B);
  and and_1 (and_1_out, C, D);
  and and_2 (and_2_out, B, C, D);
  or or_1 (b_2, not_1_out, and_1_out);
  or or_2 (c_2, and_2_out, A);

  assign a_2 = 1'b1;
  assign d_2 = 1'b0;
  assign e = 1'b1;
  assign f = 1'b1;
  assign g = 1'b1;
endmodule
